# Fritzing sketch blink4 (saved by Fritzing 0.9.0b)
breadboards: 1

parts:
  Part1 = Arduino Uno (Rev3) - ICSP
  LED2 = LED - 5mm [color="Red (633nm)" package="5 mm [THT]"]
  LED3 = LED - 5mm [color="Red (633nm)" package="5 mm [THT]"]
  LED4 = LED - 5mm [color="Red (633nm)" package="5 mm [THT]"]
  LED5 = LED - 5mm [color="Red (633nm)" package="5 mm [THT]"]
  R1 = Resistor [tolerance=±5% resistance=330 package=THT]
  R2 = Resistor [tolerance=±5% resistance=330 package=THT]
  R3 = Resistor [tolerance=±5% resistance=330 package=THT]
  R4 = Resistor [tolerance=±5% resistance=330 package=THT]

nets:
  N1: Part1.GND, R1.Pin_1, R2.Pin_1, R3.Pin_1, R4.Pin_1
  N2: Part1.D5_PWM, LED3.cathode
  N3: Part1.D6_PWM, LED2.cathode
  N4: Part1.D7, LED5.cathode
  N5: LED2.anode, R2.Pin_0
  N6: LED3.anode, R3.Pin_0
  N7: LED4.anode, R4.Pin_0
  N8: LED5.anode, R1.Pin_0
